# Fritzing sketch Mark 10 Wiring (saved by Fritzing 0.9.9b)

parts:
  Mod1 = Raspberry Pi 4B
  LED1 = LED - 5mm [color="Blue (470nm)" package="5 mm [THT]"]
  LED2 = LED - 5mm [color="Yellow (585nm)" package="5 mm [THT]"]
  LED3 = LED - 5mm [color="Green (560nm)" package="5 mm [THT]"]
  S1 = Pushbutton [package="[SMD]"]
  R1 = Resistor [tolerance=±5% resistance=330 package=THT]
  R2 = Resistor [tolerance=±5% resistance=330 package=THT]
  R3 = Resistor [tolerance=±5% resistance=330 package=THT]

nets:
  N1: Mod1.3V3, S1.Pin_3, S1.Pin_4
  N2: Mod1.GND, LED1.cathode, LED2.cathode, LED3.cathode
  N3: Mod1.GPIO16, R1.Pin_1
  N4: Mod1.GPIO26, R3.Pin_1
  N5: Mod1.GPIO20, R2.Pin_1
  N6: Mod1.GPIO21, S1.Pin_2
  N7: LED1.anode, R1.Pin_0
  N8: LED2.anode, R2.Pin_0
  N9: LED3.anode, R3.Pin_0

notes:
  Note: The long leg of the LED lights needs to be a positive voltage from the GPIO pins. The black wires are grounded connections.
  Connections:
  Blue Light (Bluetooth Light) - 36
  Yellow Light (Serial Light) - 38
  Green Light (Run/Stop Light) - 37
  Button (Stop and Start) - 40
